// Digital circuit 4-Bit-adder.dig as structural Verilog
module _4_Bit_adder (
  input  [3:0] A,
  input  [3:0] B,
  output [3:0] S,
  output C_out
);

  wire full_adder_2_co, full_adder_3_co, full_adder_4_co;

  full_adder full_adder_1 (.A(A[3]), .B(B[3]), .Ci(full_adder_2_co), .S(S[3]), .Co(C_out));
  full_adder full_adder_2 (.A(A[2]), .B(B[2]), .Ci(full_adder_3_co), .S(S[2]), .Co(full_adder_2_co));
  full_adder full_adder_3 (.A(A[1]), .B(B[1]), .Ci(full_adder_4_co), .S(S[1]), .Co(full_adder_3_co));
  full_adder full_adder_4 (.A(A[0]), .B(B[0]), .Ci(1'b0), .S(S[0]), .Co(full_adder_4_co));
endmodule
