// Digital circuit 4-Bit-register.dig as structural Verilog
module _4_Bit_register (
  input  [3:0] A,
  input  Clock,
  output [3:0] D
);

  d_flip_flop d_flip_flop_1 (.Clock(Clock), .A(A[3]), .D(D[3]));
  d_flip_flop d_flip_flop_2 (.Clock(Clock), .A(A[2]), .D(D[2]));
  d_flip_flop d_flip_flop_3 (.Clock(Clock), .A(A[1]), .D(D[1]));
  d_flip_flop d_flip_flop_4 (.Clock(Clock), .A(A[0]), .D(D[0]));
endmodule
