// Digital circuit 4-bit-counter.dig as structural Verilog
module _4_bit_counter (
  input  Inc,
  input  [3:0] JMP_in,
  input  Clock,
  output [3:0] C_out
);

  wire or_1_out;
  wire [3:0] _4_bit_adder_1_s, multiplexer_1_out;

  or or_1 (or_1_out, Inc, Clock);
  _4_Bit_register _4_bit_register_1 (.A(multiplexer_1_out), .Clock(or_1_out), .D(C_out));
  _4_Bit_adder _4_bit_adder_1 (.A(C_out), .B(4'b0001), .S(_4_bit_adder_1_s));  // open: C_out
  Multiplexer #(.Bits(4)) multiplexer_1 (.sel(Clock), .in_0(_4_bit_adder_1_s), .in_1(JMP_in), .out(multiplexer_1_out));

  // Notes on the sheet:
  //   1
endmodule
