// Digital circuit 8-Bit-RAM.dig as structural Verilog
module _8_Bit_RAM (
  input  [3:0] Address,
  input  [7:0] Data_in,
  input  Clock,
  output [7:0] Data_out
);

  wire [7:0] _8_bit_gated_register_1_d, _8_bit_gated_register_2_d, _8_bit_gated_register_3_d,
       _8_bit_gated_register_4_d, _8_bit_gated_register_5_d, _8_bit_gated_register_6_d,
       _8_bit_gated_register_7_d, _8_bit_gated_register_8_d, _8_bit_gated_register_9_d,
       _8_bit_gated_register_10_d, _8_bit_gated_register_11_d, _8_bit_gated_register_12_d,
       _8_bit_gated_register_13_d, _8_bit_gated_register_14_d, _8_bit_gated_register_15_d,
       _8_bit_gated_register_16_d;
  wire [15:0] eeprom_1_d;

  EEPROM #(.AddrBits(4), .Bits(16)) eeprom_1 (.A(Address), .CS(1'b1), .WE(1'b0), .OE(1'b1), .D(eeprom_1_d));
  _8_Bit_gated_register _8_bit_gated_register_1 (
    .A(Data_in), .Clock(Clock), .Enable(eeprom_1_d[0]), .D(_8_bit_gated_register_1_d));
  _8_Bit_gated_register _8_bit_gated_register_2 (
    .A(Data_in), .Clock(Clock), .Enable(eeprom_1_d[1]), .D(_8_bit_gated_register_2_d));
  _8_Bit_gated_register _8_bit_gated_register_3 (
    .A(Data_in), .Clock(Clock), .Enable(eeprom_1_d[2]), .D(_8_bit_gated_register_3_d));
  _8_Bit_gated_register _8_bit_gated_register_4 (
    .A(Data_in), .Clock(Clock), .Enable(eeprom_1_d[3]), .D(_8_bit_gated_register_4_d));
  _8_Bit_gated_register _8_bit_gated_register_5 (
    .A(Data_in), .Clock(Clock), .Enable(eeprom_1_d[4]), .D(_8_bit_gated_register_5_d));
  _8_Bit_gated_register _8_bit_gated_register_6 (
    .A(Data_in), .Clock(Clock), .Enable(eeprom_1_d[5]), .D(_8_bit_gated_register_6_d));
  _8_Bit_gated_register _8_bit_gated_register_7 (
    .A(Data_in), .Clock(Clock), .Enable(eeprom_1_d[6]), .D(_8_bit_gated_register_7_d));
  _8_Bit_gated_register _8_bit_gated_register_8 (
    .A(Data_in), .Clock(Clock), .Enable(eeprom_1_d[7]), .D(_8_bit_gated_register_8_d));
  _8_Bit_gated_register _8_bit_gated_register_9 (
    .A(Data_in), .Clock(Clock), .Enable(eeprom_1_d[8]), .D(_8_bit_gated_register_9_d));
  _8_Bit_gated_register _8_bit_gated_register_10 (
    .A(Data_in), .Clock(Clock), .Enable(eeprom_1_d[9]), .D(_8_bit_gated_register_10_d));
  _8_Bit_gated_register _8_bit_gated_register_11 (
    .A(Data_in), .Clock(Clock), .Enable(eeprom_1_d[10]), .D(_8_bit_gated_register_11_d));
  _8_Bit_gated_register _8_bit_gated_register_12 (
    .A(Data_in), .Clock(Clock), .Enable(eeprom_1_d[11]), .D(_8_bit_gated_register_12_d));
  _8_Bit_gated_register _8_bit_gated_register_13 (
    .A(Data_in), .Clock(Clock), .Enable(eeprom_1_d[12]), .D(_8_bit_gated_register_13_d));
  _8_Bit_gated_register _8_bit_gated_register_14 (
    .A(Data_in), .Clock(Clock), .Enable(eeprom_1_d[13]), .D(_8_bit_gated_register_14_d));
  _8_Bit_gated_register _8_bit_gated_register_15 (
    .A(Data_in), .Clock(Clock), .Enable(eeprom_1_d[14]), .D(_8_bit_gated_register_15_d));
  _8_Bit_gated_register _8_bit_gated_register_16 (
    .A(Data_in), .Clock(Clock), .Enable(eeprom_1_d[15]), .D(_8_bit_gated_register_16_d));
  assign Data_out = _8_bit_gated_register_1_d | _8_bit_gated_register_2_d | _8_bit_gated_register_3_d | _8_bit_gated_register_4_d | _8_bit_gated_register_5_d | _8_bit_gated_register_6_d | _8_bit_gated_register_7_d | _8_bit_gated_register_8_d | _8_bit_gated_register_9_d | _8_bit_gated_register_10_d | _8_bit_gated_register_11_d | _8_bit_gated_register_12_d | _8_bit_gated_register_13_d | _8_bit_gated_register_14_d | _8_bit_gated_register_15_d | _8_bit_gated_register_16_d;  // Or or_1, 8 bits wide

  // Notes on the sheet:
  //   contents of eeprom_1 (hex, n*v repeats v):
  //   1,2,4,8,10,20,40,80,100,200,400,800,1000,2000,4000,8000
endmodule
