// Digital circuit 8-Bit-adder.dig as structural Verilog
module _8_Bit_adder (
  input  [7:0] B,
  input  [7:0] A,
  input  Subtract,
  output [7:0] S,
  output Co
);

  wire full_adder_2_co, full_adder_3_co, full_adder_4_co, full_adder_5_co, full_adder_6_co, full_adder_7_co,
       full_adder_8_co, xor_1_out, xor_2_out, xor_3_out, xor_4_out, xor_5_out, xor_6_out, xor_7_out,
       xor_8_out;

  full_adder full_adder_1 (.A(A[7]), .B(xor_1_out), .Ci(full_adder_2_co), .S(S[7]), .Co(Co));
  full_adder full_adder_2 (.A(A[6]), .B(xor_3_out), .Ci(full_adder_3_co), .S(S[6]), .Co(full_adder_2_co));
  full_adder full_adder_3 (.A(A[5]), .B(xor_2_out), .Ci(full_adder_4_co), .S(S[5]), .Co(full_adder_3_co));
  full_adder full_adder_4 (.A(A[4]), .B(xor_4_out), .Ci(full_adder_5_co), .S(S[4]), .Co(full_adder_4_co));
  xor xor_1 (xor_1_out, Subtract, B[7]);
  full_adder full_adder_5 (.A(A[3]), .B(xor_5_out), .Ci(full_adder_6_co), .S(S[3]), .Co(full_adder_5_co));
  xor xor_2 (xor_2_out, Subtract, B[5]);
  xor xor_3 (xor_3_out, Subtract, B[6]);
  xor xor_4 (xor_4_out, Subtract, B[4]);
  full_adder full_adder_6 (.A(A[2]), .B(xor_7_out), .Ci(full_adder_7_co), .S(S[2]), .Co(full_adder_6_co));
  xor xor_5 (xor_5_out, Subtract, B[3]);
  full_adder full_adder_7 (.A(A[1]), .B(xor_6_out), .Ci(full_adder_8_co), .S(S[1]), .Co(full_adder_7_co));
  xor xor_6 (xor_6_out, Subtract, B[1]);
  xor xor_7 (xor_7_out, Subtract, B[2]);
  full_adder full_adder_8 (.A(A[0]), .B(xor_8_out), .Ci(Subtract), .S(S[0]), .Co(full_adder_8_co));
  xor xor_8 (xor_8_out, Subtract, B[0]);
endmodule
