// Digital circuit 8-Bit-computer.dig as structural Verilog
module _8_Bit_computer (
  input  Clock,
  input  disable_CPU,
  input  IR_out_2,
  input  IR_in_2,
  input  Display_in,
  input  RAM_out_2,
  input  RAM_in_2,
  input  MAR_in_2,
  input  PC_out,
  input  PC_inc_2,
  input  PC_in_2,
  input  ALU_out_2,
  input  Flags_in_2,
  input  SUB_2,
  input  A_out_2,
  input  B_in_2,
  input  A_in_2,
  input  in_36,
  input  in_37,
  input  in_38,
  input  in_39,
  input  in_40,
  input  in_41,
  input  in_42,
  input  in_43,
  input  Enable_User_Input,
  output Zero,
  output Carry,
  output HLT,
  output IR_out,
  output IR_in,
  output RAM_out,
  output RAM_in,
  output MAR_in,
  output PC_inc,
  output PC_in,
  output ALU_out,
  output Flags_in,
  output SUB,
  output A_out,
  output B_in,
  output A_in,
  output PC_out_2,
  output Display_in_2,
  output out_45,
  output out_46,
  output out_47,
  output out_48,
  output out_49,
  output out_50,
  output out_51,
  output out_52
);

  wire _8_bit_adder_1_co, and_1_out, and_2_out, and_3_out, and_4_out, and_5_out, and_6_out, and_7_out,
       and_8_out, and_9_out, and_10_out, and_11_out, not_1_out, not_2_out, not_3_out, not_4_out, not_5_out,
       not_6_out, not_7_out, not_8_out, not_9_out, not_10_out, not_11_out, or_1_out;
  wire [2:0] step_counter_1_step;
  wire [3:0] _4_bit_counter_1_c_out, Instruction_Register_d, MAR_d;
  wire [7:0] Display_Register_d, fgnfet_37_s, fgnfet_38_s, RAM_data_out, Register_B_d;
  wire [8:5] Instruction_Register_d_2;
  wire [15:0] eeprom_1_d;
  wire [20:0] display_eeprom_1_p2;

  and and_1 (and_1_out, PC_inc, or_1_out);
  and and_2 (and_2_out, PC_in, or_1_out);
  not not_1 (not_1_out, HLT);
  FGNFET fgnfet_1 (.G(not_3_out), .D(A_in), .S(eeprom_1_d[15]));
  FGNFET fgnfet_2 (.G(not_3_out), .D(B_in), .S(eeprom_1_d[14]));
  FGNFET fgnfet_3 (.G(not_3_out), .D(A_out), .S(eeprom_1_d[13]));
  and and_3 (and_3_out, Clock, not_1_out);
  FGNFET fgnfet_4 (.G(not_3_out), .D(SUB), .S(eeprom_1_d[12]));
  FGNFET fgnfet_5 (.G(not_3_out), .D(Flags_in), .S(eeprom_1_d[11]));
  or or_1 (or_1_out, disable_CPU, and_3_out);
  and and_4 (and_4_out, MAR_in, or_1_out);
  and and_5 (and_5_out, RAM_in, or_1_out);
  and and_6 (and_6_out, IR_in, or_1_out);
  not not_2 (not_2_out, and_3_out);
  step_counter step_counter_1 (.Clock(not_2_out), .Step(step_counter_1_step));
  FGNFET fgnfet_6 (.G(not_3_out), .D(ALU_out), .S(eeprom_1_d[10]));
  FGNFET fgnfet_7 (.G(not_3_out), .D(PC_in), .S(eeprom_1_d[9]));
  _4_bit_counter _4_bit_counter_1 (
    .Inc(and_1_out), .JMP_in({out_48, out_47, out_46, out_45}), .Clock(and_2_out),
    .C_out(_4_bit_counter_1_c_out));
  FGNFET fgnfet_8 (.G(not_3_out), .D(PC_inc), .S(eeprom_1_d[8]));
  FGNFET fgnfet_9 (.G(not_3_out), .D(PC_out_2), .S(eeprom_1_d[7]));
  FGNFET #(.Bits(4)) fgnfet_10 (.G(PC_out_2), .D(_4_bit_counter_1_c_out), .S({out_48, out_47, out_46, out_45}));
  _8_Bit_RAM RAM (
    .Address(MAR_d), .Data_in({out_52, out_51, out_50, out_49, out_48, out_47, out_46, out_45}),
    .Clock(and_5_out), .Data_out(RAM_data_out));
  EEPROM #(.AddrBits(9), .Bits(16)) eeprom_1 (
    .A({Instruction_Register_d_2, step_counter_1_step, Zero, Carry}), .CS(1'b1), .WE(1'b0), .OE(1'b1),
    .D(eeprom_1_d));
  FGNFET fgnfet_11 (.G(not_3_out), .D(MAR_in), .S(eeprom_1_d[6]));
  FGNFET fgnfet_12 (.G(not_3_out), .D(RAM_in), .S(eeprom_1_d[5]));
  _4_Bit_register MAR (.A({out_48, out_47, out_46, out_45}), .Clock(and_4_out), .D(MAR_d));
  FGNFET #(.Bits(8)) fgnfet_13 (
    .G(RAM_out), .D(RAM_data_out), .S({out_52, out_51, out_50, out_49, out_48, out_47, out_46, out_45}));
  _8_Bit_register Instruction_Register (
    .A({out_52, out_51, out_50, out_49, out_48, out_47, out_46, out_45}), .Clock(and_6_out),
    .D({Instruction_Register_d_2, Instruction_Register_d}));
  FGNFET #(.Bits(4)) fgnfet_14 (.G(IR_out), .D(Instruction_Register_d), .S({out_48, out_47, out_46, out_45}));
  FGNFET #(.Bits(4)) fgnfet_15 (.G(IR_out), .D(4'b0000), .S({out_52, out_51, out_50, out_49}));
  FGNFET fgnfet_16 (.G(not_3_out), .D(RAM_out), .S(eeprom_1_d[4]));
  FGNFET fgnfet_17 (.G(not_3_out), .D(Display_in_2), .S(eeprom_1_d[3]));
  FGNFET fgnfet_18 (.G(not_3_out), .D(IR_in), .S(eeprom_1_d[2]));
  FGNFET fgnfet_19 (.G(not_3_out), .D(IR_out), .S(eeprom_1_d[1]));
  FGNFET fgnfet_20 (.G(Enable_User_Input), .D(out_52), .S(in_43));
  FGNFET fgnfet_21 (.G(Enable_User_Input), .D(out_51), .S(in_42));
  FGNFET fgnfet_22 (.G(not_3_out), .D(HLT), .S(eeprom_1_d[0]));
  FGNFET fgnfet_23 (.G(Enable_User_Input), .D(out_50), .S(in_41));
  FGNFET fgnfet_24 (.G(Enable_User_Input), .D(out_49), .S(in_40));
  not not_3 (not_3_out, disable_CPU);
  FGNFET fgnfet_25 (.G(Enable_User_Input), .D(out_48), .S(in_39));
  FGNFET fgnfet_26 (.G(Enable_User_Input), .D(out_47), .S(in_38));
  FGNFET fgnfet_27 (.G(disable_CPU), .D(A_in), .S(A_in_2));
  FGNFET fgnfet_28 (.G(disable_CPU), .D(B_in), .S(B_in_2));
  FGNFET fgnfet_29 (.G(Enable_User_Input), .D(out_46), .S(in_37));
  FGNFET fgnfet_30 (.G(Enable_User_Input), .D(out_45), .S(in_36));
  FGNFET fgnfet_31 (.G(disable_CPU), .D(A_out), .S(A_out_2));
  FGNFET fgnfet_32 (.G(disable_CPU), .D(SUB), .S(SUB_2));
  FGNFET fgnfet_33 (.G(disable_CPU), .D(Flags_in), .S(Flags_in_2));
  FGNFET fgnfet_34 (.G(disable_CPU), .D(ALU_out), .S(ALU_out_2));
  and and_7 (and_7_out, Display_in_2, or_1_out);
  FGNFET fgnfet_35 (.G(disable_CPU), .D(PC_in), .S(PC_in_2));
  FGNFET fgnfet_36 (.G(disable_CPU), .D(PC_inc), .S(PC_inc_2));
  FGNFET #(.Bits(8)) fgnfet_37 (
    .G(ALU_out), .D({out_52, out_51, out_50, out_49, out_48, out_47, out_46, out_45}), .S(fgnfet_37_s));
  FGNFET #(.Bits(8)) fgnfet_38 (
    .G(A_out), .D({out_52, out_51, out_50, out_49, out_48, out_47, out_46, out_45}), .S(fgnfet_38_s));
  _8_Bit_register Display_Register (
    .A({out_52, out_51, out_50, out_49, out_48, out_47, out_46, out_45}), .Clock(and_7_out),
    .D(Display_Register_d));
  FGNFET fgnfet_39 (.G(disable_CPU), .D(PC_out_2), .S(PC_out));
  FGNFET fgnfet_40 (.G(disable_CPU), .D(MAR_in), .S(MAR_in_2));
  and and_8 (and_8_out, or_1_out, A_in);
  FGNFET fgnfet_41 (.G(disable_CPU), .D(RAM_in), .S(RAM_in_2));
  FGNFET fgnfet_42 (.G(disable_CPU), .D(RAM_out), .S(RAM_out_2));
  _8_Bit_register Register_A (
    .A({out_52, out_51, out_50, out_49, out_48, out_47, out_46, out_45}), .Clock(and_8_out), .D(fgnfet_38_s));
  // display_EEPROM display_eeprom_1: pin names not known; wires that end beside it: Display_Register_d, display_eeprom_1_p2
  FGNFET fgnfet_43 (.G(disable_CPU), .D(Display_in_2), .S(Display_in));
  FGNFET fgnfet_44 (.G(disable_CPU), .D(IR_in), .S(IR_in_2));
  _8_Bit_adder _8_bit_adder_1 (
    .B(Register_B_d), .A(fgnfet_38_s), .Subtract(SUB), .S(fgnfet_37_s), .Co(_8_bit_adder_1_co));
  Seven_Seg seven_seg_1 (
    .a(display_eeprom_1_p2[14]), .b(display_eeprom_1_p2[15]), .c(display_eeprom_1_p2[16]),
    .d(display_eeprom_1_p2[17]), .e(display_eeprom_1_p2[18]), .f(display_eeprom_1_p2[19]),
    .g(display_eeprom_1_p2[20]), .dp(1'b0));
  FGNFET fgnfet_45 (.G(disable_CPU), .D(IR_out), .S(IR_out_2));
  FGNFET fgnfet_46 (.G(disable_CPU), .D(HLT), .S(disable_CPU));
  not not_4 (not_4_out, fgnfet_37_s[0]);
  not not_5 (not_5_out, fgnfet_37_s[1]);
  not not_6 (not_6_out, fgnfet_37_s[2]);
  not not_7 (not_7_out, fgnfet_37_s[3]);
  not not_8 (not_8_out, fgnfet_37_s[4]);
  not not_9 (not_9_out, fgnfet_37_s[5]);
  not not_10 (not_10_out, fgnfet_37_s[6]);
  not not_11 (not_11_out, fgnfet_37_s[7]);
  Seven_Seg seven_seg_2 (
    .a(display_eeprom_1_p2[7]), .b(display_eeprom_1_p2[8]), .c(display_eeprom_1_p2[9]),
    .d(display_eeprom_1_p2[10]), .e(display_eeprom_1_p2[11]), .f(display_eeprom_1_p2[12]),
    .g(display_eeprom_1_p2[13]), .dp(1'b0));
  and and_9 (and_9_out, or_1_out, B_in);
  _8_Bit_register Register_B (
    .A({out_52, out_51, out_50, out_49, out_48, out_47, out_46, out_45}), .Clock(and_9_out), .D(Register_B_d));
  Seven_Seg seven_seg_3 (
    .a(display_eeprom_1_p2[0]), .b(display_eeprom_1_p2[1]), .c(display_eeprom_1_p2[2]),
    .d(display_eeprom_1_p2[3]), .e(display_eeprom_1_p2[4]), .f(display_eeprom_1_p2[5]),
    .g(display_eeprom_1_p2[6]), .dp(1'b0));
  and and_10 (and_10_out, not_4_out, not_5_out, not_6_out, not_7_out, not_8_out, not_9_out, not_10_out, not_11_out);
  flags_register Flags_Register (.Z_in(and_10_out), .C_in(_8_bit_adder_1_co), .Clock(and_11_out), .Z(Zero), .C(Carry));
  and and_11 (and_11_out, or_1_out, Flags_in);

  // Notes on the sheet:
  //   Clock: Hz: 20
  //   disable_CPU: default 1
  //   HLT
  //   PC inc
  //   Clock
  //   PC in
  //   Program Counter
  //   MAR in
  //   RAM in
  //   IR in
  //   opcode
  //   A in
  //   CONTROL
  //   Flags in
  //   SUB
  //   A out
  //   B in
  //   step
  //   PC out
  //   ALU out
  //   RAM
  //   IR out
  //   contents of eeprom_1 (hex, n*v repeats v):
  //   4*c0,4*114,24*0,4*c0,4*114,4*42,4*8010,16*0,4*c0,4*114,4*42,4*4010
  //   ,4*8c00,12*0,4*c0,4*114,4*42,4*4010,4*9c00,12*0,4*c0,4*114,4*42
  //   ,4*2020,16*0,4*c0,4*114,4*8002,20*0,4*c0,4*114,4*202,20*0,4*c0
  //   ,4*114,0,202,0,202,20*0,4*c0,4*114,0,0,202,202,20*0,4*c0,4*114
  //   ,4*2008,20*0,4*c0,4*114,24*0,4*c0,4*114,24*0,4*c0,4*114,24*0,4*c0
  //   ,4*114,24*0,4*c0,4*114,24*0,4*c0,4*114,4*1
  //   RAM out
  //   Display in
  //   flags
  //   Zero
  //   Carry
  //   BUS
  //   args
  //   User Input
  //   ALU
  //   DISPLAY
  //   Subtract
  //   zero
endmodule
