// Digital circuit 8-Bit-gated-register.dig as structural Verilog
module _8_Bit_gated_register (
  input  [7:0] A,
  input  Clock,
  input  Enable,
  output [7:0] D
);

  wire and_1_out;
  wire [7:0] _8_bit_register_1_d;

  and and_1 (and_1_out, Clock, Enable);
  _8_Bit_register _8_bit_register_1 (.A(A), .Clock(and_1_out), .D(_8_bit_register_1_d));
  assign D = {8{Enable}} & _8_bit_register_1_d;  // And and_2, 8 bits wide
endmodule
