// Digital circuit 8-Bit-register.dig as structural Verilog
module _8_Bit_register (
  input  [7:0] A,
  input  Clock,
  output [7:0] D
);

  _4_Bit_register _4_bit_register_1 (.A(A[7:4]), .Clock(Clock), .D(D[7:4]));
  _4_Bit_register _4_bit_register_2 (.A(A[3:0]), .Clock(Clock), .D(D[3:0]));
endmodule
