// Digital circuit d-flip-flop.dig as structural Verilog
module d_flip_flop (
  input  Clock,
  input  A,
  output D
);

  wire d_latch_1_d, delay_1_out, not_1_out;

  Delay delay_1 (.in(Clock), .out(delay_1_out));
  d_latch d_latch_1 (.Clock(delay_1_out), .A(A), .D(d_latch_1_d));
  not not_1 (not_1_out, Clock);
  d_latch d_latch_2 (.Clock(not_1_out), .A(d_latch_1_d), .D(D));
endmodule
