// Digital circuit d-latch.dig as structural Verilog
module d_latch (
  input  Clock,
  input  A,
  output D
);

  wire and_1_out, and_2_out, delay_1_out, not_1_out;

  Delay delay_1 (.in(Clock), .out(delay_1_out));
  not not_1 (not_1_out, Clock);
  and and_1 (and_1_out, D, delay_1_out);
  and and_2 (and_2_out, not_1_out, A);
  or or_1 (D, and_1_out, and_2_out);
endmodule
