// Digital circuit display-EEPROM.dig as structural Verilog
module display_EEPROM (
  input  [7:0] A,
  output [20:0] D
);

  wire [11:0] eeprom_1_d;

  EEPROM #(.AddrBits(8), .Bits(12)) eeprom_1 (.A(A), .CS(1'b1), .WE(1'b0), .OE(1'b1), .D(eeprom_1_d));
  EEPROM #(.AddrBits(4), .Bits(7)) eeprom_2 (.A(eeprom_1_d[3:0]), .CS(1'b1), .WE(1'b0), .OE(1'b1), .D(D[6:0]));
  EEPROM #(.AddrBits(4), .Bits(7)) eeprom_3 (.A(eeprom_1_d[7:4]), .CS(1'b1), .WE(1'b0), .OE(1'b1), .D(D[13:7]));
  EEPROM #(.AddrBits(4), .Bits(7)) eeprom_4 (.A(eeprom_1_d[11:8]), .CS(1'b1), .WE(1'b0), .OE(1'b1), .D(D[20:14]));
  // Pins of 12 and 21 bits meet at D

  // Notes on the sheet:
  //   contents of eeprom_1 (hex, n*v repeats v):
  //   0,1,2,3,4,5,6,7,8,9,10,11,12,13,14,15,16,17,18,19,20,21,22,23
  //   ,24,25,26,27,28,29,30,31,32,33,34,35,36,37,38,39,40,41,42,43,44
  //   ,45,46,47,48,49,50,51,52,53,54,55,56,57,58,59,60,61,62,63,64,65
  //   ,66,67,68,69,70,71,72,73,74,75,76,77,78,79,80,81,82,83,84,85,86
  //   ,87,88,89,90,91,92,93,94,95,96,97,98,99,100,101,102,103,104,105
  //   ,106,107,108,109,110,111,112,113,114,115,116,117,118,119,120,121
  //   ,122,123,124,125,126,127,128,129,130,131,132,133,134,135,136,137
  //   ,138,139,140,141,142,143,144,145,146,147,148,149,150,151,152,153
  //   ,154,155,156,157,158,159,160,161,162,163,164,165,166,167,168,169
  //   ,170,171,172,173,174,175,176,177,178,179,180,181,182,183,184,185
  //   ,186,187,188,189,190,191,192,193,194,195,196,197,198,199,200,201
  //   ,202,203,204,205,206,207,208,209,210,211,212,213,214,215,216,217
  //   ,218,219,220,221,222,223,224,225,226,227,228,229,230,231,232,233
  //   ,234,235,236,237,238,239,240,241,242,243,244,245,246,247,248,249
  //   ,250,251,252,253,254,255
  //   contents of eeprom_2 (hex, n*v repeats v):
  //   3f,6,5b,4f,66,6d,7d,7,7f,6f,77,7c,39,5e,79,71
  //   contents of eeprom_3 (hex, n*v repeats v):
  //   3f,6,5b,4f,66,6d,7d,7,7f,6f,77,7c,39,5e,79,71
  //   contents of eeprom_4 (hex, n*v repeats v):
  //   3f,6,5b,4f,66,6d,7d,7,7f,6f,77,7c,39,5e,79,71
endmodule
