// Digital circuit flags-register.dig as structural Verilog
module flags_register (
  input  Z_in,
  input  C_in,
  input  Clock,
  output Z,
  output C
);

  d_flip_flop d_flip_flop_1 (.Clock(Clock), .A(C_in), .D(C));
  d_flip_flop d_flip_flop_2 (.Clock(Clock), .A(Z_in), .D(Z));
endmodule
