// Digital circuit full-adder.dig as structural Verilog
module full_adder (
  input  A,
  input  B,
  input  Ci,
  output S,
  output Co
);

  wire half_adder_1_c, half_adder_1_s, half_adder_2_c;

  half_adder half_adder_1 (.A(A), .B(B), .S(half_adder_1_s), .C(half_adder_1_c));
  half_adder half_adder_2 (.A(half_adder_1_s), .B(Ci), .S(S), .C(half_adder_2_c));
  or or_1 (Co, half_adder_2_c, half_adder_1_c);
endmodule
