// Digital circuit step-counter.dig as structural Verilog
module step_counter (
  input  Clock,
  output [2:0] Step
);

  wire not_1_out, not_2_out;
  wire [3:0] _4_bit_adder_1_s, _4_bit_register_1_d, and_2_out, and_3_out, not_3_out;
  wire [3:3] and_1_out, or_1_out;

  _4_Bit_register _4_bit_register_1 (.A(_4_bit_adder_1_s), .Clock(Clock), .D(_4_bit_register_1_d));
  not not_1 (not_1_out, _4_bit_register_1_d[1]);
  not not_2 (not_2_out, _4_bit_register_1_d[3]);
  and and_1 (and_1_out[3], _4_bit_register_1_d[0], not_1_out, _4_bit_register_1_d[2], not_2_out);
  _4_Bit_adder _4_bit_adder_1 (.A({or_1_out[3], Step}), .B(4'b0001), .S(_4_bit_adder_1_s));  // open: C_out
  assign not_3_out = ~{4{and_1_out[3]}};  // Not not_3, 4 bits wide
  assign and_2_out = 4'b0000 & {4{and_1_out[3]}};  // And and_2, 4 bits wide
  assign and_3_out = not_3_out & _4_bit_register_1_d;  // And and_3, 4 bits wide
  assign {or_1_out[3], Step} = and_2_out | and_3_out;  // Or or_1, 4 bits wide

  // Notes on the sheet:
  //   1
endmodule
